# Fritzing sketch Component_Design (saved by Fritzing 0.9.6b)

parts:
  Mod1 = Raspberry Pi Pico
  OLED1 = OLED 128x64 I2C Monochrome Display
  M1 = BMP280
  LED1 = smd LED [color="Red (633nm)" package="0805 [SMD]"]
  LED2 = smd LED [color="Blue (470nm)" package="0805 [SMD]"]
  R1 = Resistor [tolerance=±5% resistance=220 package="2010 [SMD]"]
  R2 = Resistor [tolerance=±5% resistance=220 package="2010 [SMD]"]

nets:
  N1: Mod1.pin_1, OLED1.SDA
  N2: Mod1.pin_2, OLED1.SCK
  N3: Mod1.pin_4, M1.SDA
  N4: Mod1.pin_5, M1.SCL
  GND: Mod1.pin_8, Mod1.pin_13, Mod1.pin_18, Mod1.pin_23, Mod1.pin_38, Mod1.pin_42, OLED1.GND, M1.GND, LED1.cathode, LED2.cathode
  N5: Mod1.pin_19, R1.Pin_1
  N6: Mod1.pin_20, R2.Pin_1
  VDD: Mod1.pin_36, OLED1.VDD, M1.VIN

custom parts:
  Raspberry Pi Pico: Raspberry Pi Pico. Based around the RP2040 microcontroller the Pico is a low cost microcontroller device bringing Raspberry Pi quality, cost, and easy of use to the microcontroller space. Jan 2021, Split part in to two versions: SMD (this one) and tht. This one is single sided and uses the castellation pads to solder the module to the board (no holes, other than for the USB connector!). The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
  BMP280: Temperature Humidity Barometric presure Sensor, I2C
